# Fritzing sketch 1.a.i.11_voltage-regulation (saved by Fritzing 0.9.0b)
breadboards: 1

parts:
  U1 = LIPO-2000mAh [package=lipo-2000]
  U5 = SPX29302 [package=q5-dd_spx29300]  # not connected
  Part1 = Pololu 12V Step-Down Regulator  # not connected
  Part2 = Pololu 5V Step-Up Regulator

nets:
  N1: U1.+, Part2.VIN
  N2: U1.-, Part2.GND

notes:
  12V
  5V
  5V step-down
  5V step-up
  variable voltage regulator
  Touch to VOUT
  Touch to ground
