# Fritzing sketch 1.a.i.6_led-current-limiter (saved by Fritzing 0.9.0b)
breadboards: 1

parts:
  LED1 = LEDs [package=led10mm]
  U1 = POT [package=3362u]
  V1 = DC Power [voltage=5]

nets:
  N1: LED1.A, U1.S
  N2: LED1.C, V1.V-
  N3: U1.E, V1.V+

notes:
  5V
