# Fritzing sketch 1.a.i.8_pressure-pad-with-bias-resistor (saved by Fritzing 0.9.0b)
breadboards: 1

parts:
  V1 = DC Power [voltage=5]
  R1 = Resistor [package="0402 [SMD]"]
  R2 = Resistor [package="0402 [SMD]"]

nets:
  N1: V1.V+, R1.Pin_0
  N2: V1.V-, R2.Pin_1
  N3: R1.Pin_1, R2.Pin_0

notes:
  5V
  2.4V
  pressure pad
  bias resistor
