# Fritzing sketch 1.a.ii.1_relay-driver (saved by Fritzing 0.9.0b)
breadboards: 1

parts:
  U1 = RELAY [package=relay-g5q]
  V1 = DC Power [voltage=5]
  V2 = DC Power [voltage=3V]
  M1 = DC Motor
  LED1 = smd LED [color="Red (633nm)" package="0805 [SMD]"]

nets:
  N1: U1.COIL2, V1.V-
  N2: U1.MAIN, V2.V+
  N3: U1.NO, M1.pin_1
  N4: U1.NC, LED1.anode
  N5: U1.COIL1, V1.V+
  N6: V2.V-, M1.pin_2, LED1.cathode

notes:
  3V
  5V
  .21A
  .3A
