# Fritzing sketch 1.a.ii.4_transistor-and-sensor-for-power (saved by Fritzing 0.9.0b)
breadboards: 1

parts:
  M1 = DC Motor
  Q1 = TRANSISTOR_PNP [package=to-92]
  V1 = DC Power [voltage=5]
  R1 = PHOTOCELL [package=photocell-kit]
  V2 = DC Power [voltage=2]

nets:
  N1: M1.pin_1, V2.V+
  N2: M1.pin_2, Q1.C
  N3: Q1.E, V1.V-, V2.V-
  N4: Q1.B, R1.P$2
  N5: V1.V+, R1.P$1

notes:
  2.0V
  .17A
  5.0V
  .01A
